// Logisim project Lab-09.circ as structural Verilog: 5 circuits, main circuit main
module main (
  input  Ak,
  input  E,
  input  F,
  input  Bk,
  input  i0,
  input  i1,
  input  i2,
  input  i3,
  input  A3,
  input  A2,
  input  A1,
  input  A0,
  input  [1:0] A_B,
  input  Ck,
  input  Carry,
  input  [1:0] in_16,
  input  B3,
  input  B2,
  input  B1,
  input  B0,
  input  A3_2,
  input  A2_2,
  input  A1_2,
  input  A0_2,
  input  S,
  input  Ak_2,
  input  [1:0] A_B_2,
  input  B3_2,
  input  B2_2,
  input  B1_2,
  input  B0_2,
  input  Carry_2,
  input  Bk_2,
  input  [1:0] A_B_3,
  input  Carry_3,
  input  [2:0] in_36,
  input  D,
  input  _0,
  input  _1,
  input  [2:0] A_B_C,
  output S_2,
  output Ck_2,
  output C,
  output S3,
  output S2,
  output S1,
  output S0,
  output C_2,
  output S0_2,
  output S3_2,
  output S2_2,
  output S1_2,
  output S0_3,
  output C_3,
  output S_3,
  output C_4,
  output Sk,
  output Sk_2,
  output Ck_3,
  output S_4,
  output C_5,
  output out_62,
  output F_2
);

  wire _0_out, _1_out, _2_out, _3_out, and_1_out, and_2_out, and_3_out, and_4_out, and_5_out, decoder_1_out1,
       decoder_1_out2, decoder_1_out3, decoder_1_out4, decoder_1_out5, decoder_1_out6, decoder_1_out7,
       decoder_2_out0, decoder_2_out1, decoder_2_out2, decoder_2_out3, decoder_3_out0, decoder_3_out1,
       decoder_3_out2, decoder_3_out3, decoder_3_out4, decoder_3_out5, decoder_3_out6, decoder_4_out1,
       decoder_4_out2, decoder_4_out3, decoder_4_out4, decoder_4_out5, decoder_4_out6, decoder_4_out7,
       full_adder_1_cip1, full_adder_2_cip1, full_adder_4_cip1, full_adder_5_cip1, full_adder_6_cip1,
       half_adder_1_ck, nand_1_out, nand_2_out, nand_3_out, nand_4_out, nand_5_out, nand_8_out, nand_9_out,
       nand_10_out, nand_11_out, nand_12_out, nand_13_out, nand_14_out, nand_15_out, nand_16_out,
       nand_18_out, nand_19_out, nand_20_out, nand_21_out, nand_23_out, nor_1_out, not_1_out, not_2_out,
       not_3_out, or_4_out, xnor_1_out, xor_1_out;

  nand nand_1 (nand_1_out, Ak_2, Ak_2);
  nand nand_2 (nand_2_out, Bk_2, Bk_2);
  nand nand_3 (nand_3_out, Ak_2, Bk_2);
  Decoder #(.select(3), .enable("false")) decoder_1 (
    .out1(decoder_1_out1), .out2(decoder_1_out2), .out3(decoder_1_out3), .out4(decoder_1_out4),
    .out5(decoder_1_out5), .out6(decoder_1_out6), .out7(decoder_1_out7), .sel({Carry_3, A_B_3}));  // open: out0
  not not_1 (not_1_out, D);
  nand nand_4 (nand_4_out, nand_1_out, Bk_2);
  nand nand_5 (nand_5_out, Ak_2, nand_2_out);
  nand nand_6 (Ck_3, nand_3_out, nand_3_out);
  Multiplexer #(.select(3), .enable("false")) multiplexer_1 (
    .in0(not_1_out), .in1(_0), .in2(not_1_out), .in3(_0), .in4(_1), .in5(D), .in6(_1), .in7(_1), .out(F_2),
    .sel(A_B_C));
  Half_Adder half_adder_1 (.Ak(A0), .Bk(B0), .Sk(S0), .Ck(half_adder_1_ck));
  Full_Adder full_adder_1 (.Ai(A1), .Bi(B1), .Ci(half_adder_1_ck), .Si(S1), .Cip1(full_adder_1_cip1));
  Full_Adder full_adder_2 (.Ai(A2), .Bi(B2), .Ci(full_adder_1_cip1), .Si(S2), .Cip1(full_adder_2_cip1));
  Full_Adder full_adder_3 (.Ai(A3), .Bi(B3), .Ci(full_adder_2_cip1), .Si(S3), .Cip1(C_2));
  nand nand_7 (Sk_2, nand_4_out, nand_5_out);
  or or_1 (S_4, decoder_1_out1, decoder_1_out2, decoder_1_out4, decoder_1_out7);
  or or_2 (C_5, decoder_1_out3, decoder_1_out5, decoder_1_out6, decoder_1_out7);
  nand nand_8 (nand_8_out, Bk, Ck);
  nand nand_9 (nand_9_out, Ak, Ck);
  nand nand_10 (nand_10_out, Ak, Bk);
  nand nand_11 (nand_11_out, Ak, Ak);
  nand nand_12 (nand_12_out, Bk, Bk);
  nand nand_13 (nand_13_out, Ak, Ak);
  nand nand_14 (nand_14_out, Ck, Ck);
  nand nand_15 (nand_15_out, Bk, Bk);
  nand nand_16 (nand_16_out, Ck, Ck);
  nand nand_17 (Ck_2, nand_8_out, nand_9_out, nand_10_out);
  nand nand_18 (nand_18_out, nand_11_out, nand_12_out, Ck);
  nand nand_19 (nand_19_out, nand_13_out, Bk, nand_14_out);
  nand nand_20 (nand_20_out, Ak, nand_15_out, nand_16_out);
  nand nand_21 (nand_21_out, Ak, Bk, Ck);
  nand nand_22 (Sk, nand_18_out, nand_19_out, nand_20_out, nand_21_out);
  Decoder #(.select(2), .enable("false")) decoder_2 (
    .out0(decoder_2_out0), .out1(decoder_2_out1), .out2(decoder_2_out2), .out3(decoder_2_out3), .sel(in_16));
  and and_1 (and_1_out, decoder_2_out0, i3);
  and and_2 (and_2_out, decoder_2_out1, i2);
  and and_3 (and_3_out, decoder_2_out2, i1);
  and and_4 (and_4_out, decoder_2_out3, i0);
  or or_3 (S0_2, and_1_out, and_2_out, and_3_out, and_4_out);
  and and_5 (and_5_out, E, E);
  or or_4 (or_4_out, E, E);
  nand nand_23 (nand_23_out, E, E);
  nor nor_1 (nor_1_out, E, E);
  xor xor_1 (xor_1_out, E, E);
  xnor xnor_1 (xnor_1_out, E, E);
  not not_2 (not_2_out, E);
  not not_3 (not_3_out, E);
  Multiplexer #(.select(3), .enable("false")) multiplexer_2 (
    .in0(not_2_out), .in1(not_3_out), .in2(and_5_out), .in3(or_4_out), .in4(nand_23_out), .in5(nor_1_out),
    .in6(xor_1_out), .in7(xnor_1_out), .out(out_62), .sel(in_36));
  Decoder #(.select(3), .enable("false")) decoder_3 (
    .out0(decoder_3_out0), .out1(decoder_3_out1), .out2(decoder_3_out2), .out3(decoder_3_out3),
    .out4(decoder_3_out4), .out5(decoder_3_out5), .out6(decoder_3_out6), .sel({Carry, A_B}));  // open: out7
  Decoder #(.select(3), .enable("false")) decoder_4 (
    .out1(decoder_4_out1), .out2(decoder_4_out2), .out3(decoder_4_out3), .out4(decoder_4_out4),
    .out5(decoder_4_out5), .out6(decoder_4_out6), .out7(decoder_4_out7), .sel({Carry_2, A_B_2}));  // open: out0
  nor nor_2 (S_2, decoder_3_out0, decoder_3_out3, decoder_3_out5, decoder_3_out6);
  nor nor_3 (C, decoder_3_out0, decoder_3_out1, decoder_3_out2, decoder_3_out4);
  or or_5 (S_3, decoder_4_out1, decoder_4_out2, decoder_4_out4, decoder_4_out7);
  or or_6 (C_4, decoder_4_out3, decoder_4_out5, decoder_4_out6, decoder_4_out7);
  xor u__0 (_0_out, B0_2, S);
  xor u__1 (_1_out, B1_2, S);
  xor _2 (_2_out, B2_2, S);
  xor _3 (_3_out, B3_2, S);
  Full_Adder full_adder_4 (.Ai(A0_2), .Bi(_0_out), .Ci(S), .Si(S0_3), .Cip1(full_adder_4_cip1));
  Full_Adder full_adder_5 (.Ai(A1_2), .Bi(_1_out), .Ci(full_adder_4_cip1), .Si(S1_2), .Cip1(full_adder_5_cip1));
  Full_Adder full_adder_6 (.Ai(A2_2), .Bi(_3_out), .Ci(full_adder_5_cip1), .Si(S2_2), .Cip1(full_adder_6_cip1));
  Full_Adder full_adder_7 (.Ai(A3_2), .Bi(_2_out), .Ci(full_adder_6_cip1), .Si(S3_2), .Cip1(C_3));

  assign F = E;

  // Notes on the sheet:
  //   Ex 1) In Class
  //   Ex. 2) In Class
  //   Ex. 3) In Class
  //   Ex. 4) In Class
  //   Ex. 1) Homework
  //   Ex 2) Homework
  //   Ex. 3) Homework
  //   Ex. 4) Homework
  //   Ex. 5) Homework
endmodule

module Half_Adder (
  input  Ak,
  input  Bk,
  output Sk,
  output Ck
);

  wire and_2_out, and_3_out, not_1_out, not_2_out;

  not not_1 (not_1_out, Ak);
  not not_2 (not_2_out, Bk);
  and and_1 (Ck, Ak, Bk);
  and and_2 (and_2_out, not_1_out, Bk);
  and and_3 (and_3_out, Ak, not_2_out);
  or or_1 (Sk, and_2_out, and_3_out);
endmodule

module Full_Adder (
  input  Ai,
  input  Bi,
  input  Ci,
  output Si,
  output Cip1
);

  wire and_1_out, and_2_out, and_3_out, and_4_out, and_5_out, and_6_out, and_7_out, not_1_out, not_2_out,
       not_3_out, not_4_out, not_5_out, not_6_out;

  not not_1 (not_1_out, Ai);
  not not_2 (not_2_out, Bi);
  not not_3 (not_3_out, Ai);
  not not_4 (not_4_out, Ci);
  not not_5 (not_5_out, Bi);
  not not_6 (not_6_out, Ci);
  and and_1 (and_1_out, Bi, Ci);
  and and_2 (and_2_out, Ai, Ci);
  and and_3 (and_3_out, Ai, Bi);
  and and_4 (and_4_out, not_1_out, not_2_out, Ci);
  and and_5 (and_5_out, not_3_out, Bi, not_4_out);
  and and_6 (and_6_out, Ai, not_5_out, not_6_out);
  and and_7 (and_7_out, Ai, Bi, Ci);
  or or_1 (Cip1, and_1_out, and_2_out, and_3_out);
  or or_2 (Si, and_4_out, and_5_out, and_6_out, and_7_out);
endmodule

module _1_Bit_Full_NAND (
  input  Ak,
  input  Bk,
  input  Ck,
  output Ck_2,
  output Sk
);

  wire nand_1_out, nand_2_out, nand_3_out, nand_4_out, nand_5_out, nand_6_out, nand_7_out, nand_8_out,
       nand_9_out, nand_11_out, nand_12_out, nand_13_out, nand_14_out;

  nand nand_1 (nand_1_out, Bk, Ck);
  nand nand_2 (nand_2_out, Ak, Ck);
  nand nand_3 (nand_3_out, Ak, Bk);
  nand nand_4 (nand_4_out, Ak, Ak);
  nand nand_5 (nand_5_out, Bk, Bk);
  nand nand_6 (nand_6_out, Ak, Ak);
  nand nand_7 (nand_7_out, Ck, Ck);
  nand nand_8 (nand_8_out, Bk, Bk);
  nand nand_9 (nand_9_out, Ck, Ck);
  nand nand_10 (Ck_2, nand_1_out, nand_2_out, nand_3_out);
  nand nand_11 (nand_11_out, nand_4_out, nand_5_out, Ck);
  nand nand_12 (nand_12_out, nand_6_out, Bk, nand_7_out);
  nand nand_13 (nand_13_out, Ak, nand_8_out, nand_9_out);
  nand nand_14 (nand_14_out, Ak, Bk, Ck);
  nand nand_15 (Sk, nand_11_out, nand_12_out, nand_13_out, nand_14_out);
endmodule

module Half_Adder_NAND (
  input  Ak,
  input  Bk,
  output Sk,
  output Ck
);

  wire nand_1_out, nand_2_out, nand_3_out, nand_4_out, nand_5_out;

  nand nand_1 (nand_1_out, Ak, Ak);
  nand nand_2 (nand_2_out, Bk, Bk);
  nand nand_3 (nand_3_out, Ak, Bk);
  nand nand_4 (nand_4_out, nand_1_out, Bk);
  nand nand_5 (nand_5_out, Ak, nand_2_out);
  nand nand_6 (Ck, nand_3_out, nand_3_out);
  nand nand_7 (Sk, nand_4_out, nand_5_out);
endmodule
