// Logisim project Lab-10.circ as structural Verilog: 1 circuit, main circuit main
module main (
  input  A,
  input  B,
  input  C,
  input  D,
  input  A_2,
  input  B_2,
  input  C_2,
  input  D_2
);

  wire a_2_out, a_out, aB_2_out, Ab_3_out, AB_4_out, ab_5_out, aB_6_out, Ab_7_out, AB_8_out, ab_out,
       aBc_2_out, Abc_3_out, aBc_4_out, Abc_out, abd_2_out, aBD_3_out, abd_4_out, aBD_out, ac_2_out,
       AC_3_out, Ac_4_out, aC_5_out, ac_6_out, AC_7_out, Ac_8_out, aC_out, aCD_2_out, AcD_3_out, acd_4_out,
       aCD_5_out, AcD_6_out, acd_out, aD_2_out, AD_3_out, Ad_4_out, aD_5_out, AD_6_out, Ad_out, b_2_out,
       b_out, bC_2_out, BC_3_out, bC_4_out, BC_out, BcD_2_out, BCd_3_out, bCD_4_out, BcD_5_out, BCd_6_out,
       bCD_out, Bd_2_out, bd_3_out, Bd_4_out, bd_out, c_2_out, c_out, Cd_2_out, cd_3_out, cD_4_out, Cd_5_out,
       cd_6_out, cD_out, clock_1_out, d_2_out, d_out, e_2_out, e_out, f_2_out, f_out, g_2_out, g_out,
       j_k_ff_1_q, j_k_ff_2_q, j_k_ff_3_q, j_k_ff_4_q, not_1_out, not_2_out, not_3_out, not_4_out, not_5_out,
       not_6_out, not_7_out, not_8_out;

  not not_1 (not_1_out, A);
  not not_2 (not_2_out, B);
  not not_3 (not_3_out, C);
  not not_4 (not_4_out, D);
  and bd (bd_out, not_2_out, not_4_out);
  and aC (aC_out, not_1_out, C);
  and BC (BC_out, B, C);
  and Ad (Ad_out, A, not_4_out);
  and ab (ab_out, not_1_out, not_2_out);
  and ac_2 (ac_2_out, not_1_out, not_3_out);
  and aD_2 (aD_2_out, not_1_out, D);
  and cD (cD_out, not_3_out, D);
  and aB_2 (aB_2_out, not_1_out, B);
  and Ab_3 (Ab_3_out, A, not_2_out);
  and Cd_2 (Cd_2_out, C, not_4_out);
  and AC_3 (AC_3_out, A, C);
  and AB_4 (AB_4_out, A, B);
  and cd_3 (cd_3_out, not_3_out, not_4_out);
  and Bd_2 (Bd_2_out, B, not_4_out);
  and bC_2 (bC_2_out, not_2_out, C);
  and AD_3 (AD_3_out, A, D);
  and aBD (aBD_out, not_1_out, B, D);
  and Abc (Abc_out, A, not_2_out, not_3_out);
  and acd (acd_out, not_1_out, not_3_out, not_4_out);
  and aCD_2 (aCD_2_out, not_1_out, C, D);
  and AcD_3 (AcD_3_out, A, not_3_out, D);
  and abd_2 (abd_2_out, not_1_out, not_2_out, not_4_out);
  and bCD (bCD_out, not_2_out, C, D);
  and BcD_2 (BcD_2_out, B, not_3_out, D);
  and BCd_3 (BCd_3_out, B, C, not_4_out);
  and aBc_2 (aBc_2_out, not_1_out, B, not_3_out);
  and Ac_4 (Ac_4_out, not_3_out, A);
  or u_a (a_out, bd_out, aC_out, aBD_out, BC_out, Abc_out, Ad_out);
  or u_b (b_out, ab_out, acd_out, bd_out, aCD_2_out, AcD_3_out);
  or u_c (c_out, ac_2_out, aD_2_out, cD_out, aB_2_out, Ab_3_out);
  or u_d (d_out, abd_2_out, bCD_out, BcD_2_out, BCd_3_out, Ac_4_out);
  or e (e_out, bd_out, Cd_2_out, AC_3_out, AB_4_out);
  or f (f_out, cd_3_out, aBc_2_out, Bd_2_out, Ab_3_out, AC_3_out);
  or g (g_out, bC_2_out, Cd_2_out, aBc_2_out, Ab_3_out, AD_3_out);
  _7_Segment_Display u_7_segment_display_1 (
    .g(g_out), .f(f_out), .a(a_out), .b(b_out), .e(e_out), .d(d_out), .c(c_out));  // open: dp
  Clock clock_1 (.out(clock_1_out));
  J_K_Flip_Flop j_k_ff_1 (.J(1'b1), .clk(clock_1_out), .K(1'b1), .Q(j_k_ff_1_q));  // open: Qn, preset, en, reset
  J_K_Flip_Flop j_k_ff_2 (.J(1'b1), .clk(j_k_ff_1_q), .K(1'b1), .Q(j_k_ff_2_q));  // open: Qn, preset, en, reset
  J_K_Flip_Flop j_k_ff_3 (.J(1'b1), .clk(j_k_ff_2_q), .K(1'b1), .Q(j_k_ff_3_q));  // open: Qn, preset, en, reset
  J_K_Flip_Flop j_k_ff_4 (.J(1'b1), .clk(j_k_ff_3_q), .K(1'b1), .Q(j_k_ff_4_q));  // open: Qn, preset, en, reset
  not not_5 (not_5_out, j_k_ff_3_q);
  not not_6 (not_6_out, j_k_ff_4_q);
  not not_7 (not_7_out, j_k_ff_2_q);
  not not_8 (not_8_out, j_k_ff_1_q);
  and bd_3 (bd_3_out, not_5_out, not_8_out);
  and aC_5 (aC_5_out, not_6_out, j_k_ff_2_q);
  and BC_3 (BC_3_out, j_k_ff_3_q, j_k_ff_2_q);
  and Ad_4 (Ad_4_out, j_k_ff_4_q, not_8_out);
  and ab_5 (ab_5_out, not_6_out, not_5_out);
  and ac_6 (ac_6_out, not_6_out, not_7_out);
  and aD_5 (aD_5_out, not_6_out, j_k_ff_1_q);
  and cD_4 (cD_4_out, not_7_out, j_k_ff_1_q);
  and aB_6 (aB_6_out, not_6_out, j_k_ff_3_q);
  and Ab_7 (Ab_7_out, j_k_ff_4_q, not_5_out);
  and Cd_5 (Cd_5_out, j_k_ff_2_q, not_8_out);
  and AC_7 (AC_7_out, j_k_ff_4_q, j_k_ff_2_q);
  and AB_8 (AB_8_out, j_k_ff_4_q, j_k_ff_3_q);
  and cd_6 (cd_6_out, not_7_out, not_8_out);
  and Bd_4 (Bd_4_out, j_k_ff_3_q, not_8_out);
  and bC_4 (bC_4_out, not_5_out, j_k_ff_2_q);
  and AD_6 (AD_6_out, j_k_ff_4_q, j_k_ff_1_q);
  and aBD_3 (aBD_3_out, not_6_out, j_k_ff_3_q, j_k_ff_1_q);
  and Abc_3 (Abc_3_out, j_k_ff_4_q, not_5_out, not_7_out);
  and acd_4 (acd_4_out, not_6_out, not_7_out, not_8_out);
  and aCD_5 (aCD_5_out, not_6_out, j_k_ff_2_q, j_k_ff_1_q);
  and AcD_6 (AcD_6_out, j_k_ff_4_q, not_7_out, j_k_ff_1_q);
  and abd_4 (abd_4_out, not_6_out, not_5_out, not_8_out);
  and bCD_4 (bCD_4_out, not_5_out, j_k_ff_2_q, j_k_ff_1_q);
  and BcD_5 (BcD_5_out, j_k_ff_3_q, not_7_out, j_k_ff_1_q);
  and BCd_6 (BCd_6_out, j_k_ff_3_q, j_k_ff_2_q, not_8_out);
  and aBc_4 (aBc_4_out, not_6_out, j_k_ff_3_q, not_7_out);
  and Ac_8 (Ac_8_out, not_7_out, j_k_ff_4_q);
  or u_a_2 (a_2_out, bd_3_out, aC_5_out, aBD_3_out, BC_3_out, Abc_3_out, Ad_4_out);
  or u_b_2 (b_2_out, ab_5_out, acd_4_out, bd_3_out, aCD_5_out, AcD_6_out);
  or u_c_2 (c_2_out, ac_6_out, aD_5_out, cD_4_out, aB_6_out, Ab_7_out);
  or u_d_2 (d_2_out, abd_4_out, bCD_4_out, BcD_5_out, BCd_6_out, Ac_8_out);
  or e_2 (e_2_out, bd_3_out, Cd_5_out, AC_7_out, AB_8_out);
  or f_2 (f_2_out, cd_6_out, aBc_4_out, Bd_4_out, Ab_7_out, AC_7_out);
  or g_2 (g_2_out, bC_4_out, Cd_5_out, aBc_4_out, Ab_7_out, AD_6_out);
  _7_Segment_Display u_7_segment_display_2 (
    .g(g_2_out), .f(f_2_out), .a(a_2_out), .b(b_2_out), .e(e_2_out), .d(d_2_out), .c(c_2_out));  // open: dp

  // Notes on the sheet:
  //   Lab Ex. 2 Hexa
  //   Lab Ex. 2 Hexa
endmodule
