// Logisim project Lab-11.circ as structural Verilog: 4 circuits, main circuit main
module main (
  input  D0,
  input  D1,
  input  C,
  input  D2,
  input  D3,
  input  in_6,
  input  in_7,
  input  in_8,
  input  in_9,
  input  in_10,
  input  in_11,
  input  in_12,
  input  in_13,
  input  [7:0] in_14,
  input  in_15,
  input  in_16,
  input  [3:0] in_17,
  input  L,
  input  [3:0] in_19,
  input  L___0_R___1,
  input  in_21,
  input  in_22,
  output Q0,
  output Q1,
  output Q2,
  output Q3,
  output [7:0] out_27,
  output Q0_2,
  output Q1_2,
  output Q2_2,
  output Q3_2,
  output [3:0] out_32,
  output [3:0] Right,
  output [3:0] Left
);

  wire button_out, C_out, clock_1_out, clock_2_out, clock_3_out, clock_4_out, not_1_out, not_2_out,
       not_3_out, not_4_out, not_5_out, not_6_out, not_7_out, or_1_out, parallel_1_out_5, parallel_2_out_5,
       parallel_3_out_5, parallel_4_out_5, r_l_1_out_5, r_l_2_out_5, r_l_3_out_5, r_l_4_out_5;
  wire [3:0] button_2_out, calc_1_out_12, calc_1_out_13;

  Clock clock_1 (.out(clock_1_out));
  Clock clock_2 (.out(clock_2_out));
  not not_1 (not_1_out, L);
  Clock u_C (.out(C_out));
  Clock clock_3 (.out(clock_3_out));
  D_Flip_Flop d_ff_1 (.clk(clock_1_out), .D(D0), .Q(Q0));  // open: Qn, preset, en, reset
  D_Flip_Flop d_ff_2 (.clk(clock_1_out), .D(D1), .Q(Q1));  // open: Qn, preset, en, reset
  D_Flip_Flop d_ff_3 (.clk(clock_1_out), .D(D2), .Q(Q2));  // open: Qn, preset, en, reset
  D_Flip_Flop d_ff_4 (.clk(clock_1_out), .D(D3), .Q(Q3));  // open: Qn, preset, en, reset
  Clock clock_4 (.out(clock_4_out));
  Parallel parallel_1 (.Qin(out_32[0]), .nLoad(not_1_out), .D(in_19[0]), .Load(L), .out_5(parallel_1_out_5));
  Parallel parallel_2 (.Qin(out_32[1]), .nLoad(not_1_out), .D(in_19[1]), .Load(L), .out_5(parallel_2_out_5));
  Parallel parallel_3 (.Qin(out_32[2]), .nLoad(not_1_out), .D(in_19[2]), .Load(L), .out_5(parallel_3_out_5));
  Parallel parallel_4 (.Qin(out_32[3]), .nLoad(not_1_out), .D(in_19[3]), .Load(L), .out_5(parallel_4_out_5));
  not not_2 (not_2_out, r_l_2_out_5);
  Register register_1 (.D(in_14), .Q(out_27), .clk(clock_4_out), .clr(in_15));  // open: en
  not not_3 (not_3_out, in_16);
  D_Flip_Flop d_ff_5 (.clk(or_1_out), .D(in_17[0]), .Q(Q0_2));  // open: Qn, preset, en, reset
  D_Flip_Flop d_ff_6 (.clk(or_1_out), .D(in_17[1]), .Q(Q1_2));  // open: Qn, preset, en, reset
  D_Flip_Flop d_ff_7 (.clk(or_1_out), .D(in_17[2]), .Q(Q2_2));  // open: Qn, preset, en, reset
  D_Flip_Flop d_ff_8 (.clk(or_1_out), .D(in_17[3]), .Q(Q3_2));  // open: Qn, preset, en, reset
  D_Flip_Flop d_ff_9 (.clk(C_out), .D(parallel_1_out_5), .Q(out_32[0]));  // open: Qn, preset, en, reset
  D_Flip_Flop d_ff_10 (.clk(C_out), .D(parallel_2_out_5), .Q(out_32[1]));  // open: Qn, preset, en, reset
  D_Flip_Flop d_ff_11 (.clk(C_out), .D(parallel_3_out_5), .Q(out_32[2]));  // open: Qn, preset, en, reset
  D_Flip_Flop d_ff_12 (.clk(C_out), .D(parallel_4_out_5), .Q(out_32[3]));  // open: Qn, preset, en, reset
  J_K_Flip_Flop j_k_ff_1 (
    .J(r_l_2_out_5), .clk(clock_3_out), .K(not_2_out), .Q(Left[3]));  // open: Qn, preset, en, reset
  not not_4 (not_4_out, r_l_1_out_5);
  or or_1 (or_1_out, clock_2_out, not_3_out);
  J_K_Flip_Flop j_k_ff_2 (
    .J(r_l_1_out_5), .clk(clock_3_out), .K(not_4_out), .Q(Left[2]));  // open: Qn, preset, en, reset
  not not_5 (not_5_out, r_l_3_out_5);
  J_K_Flip_Flop j_k_ff_3 (
    .J(r_l_3_out_5), .clk(clock_3_out), .K(not_5_out), .Q(Left[1]));  // open: Qn, preset, en, reset
  R_L r_l_1 (.L(Left[1]), .nR(not_7_out), .L_2(L___0_R___1), .R(Left[1]), .out_5(r_l_1_out_5));
  R_L r_l_2 (.L(in_21), .nR(not_7_out), .L_2(L___0_R___1), .R(Left[2]), .out_5(r_l_2_out_5));
  J_K_Flip_Flop j_k_ff_4 (
    .J(r_l_4_out_5), .clk(clock_3_out), .K(not_6_out), .Q(Left[0]));  // open: Qn, preset, en, reset
  not not_6 (not_6_out, r_l_4_out_5);
  Hex_Digit_Display hex_digit_display_1 (.value(calc_1_out_13));  // open: dp
  R_L r_l_3 (.L(Left[2]), .nR(not_7_out), .L_2(L___0_R___1), .R(Left[1]), .out_5(r_l_3_out_5));
  Hex_Digit_Display hex_digit_display_2 (.value(calc_1_out_12));  // open: dp
  not not_7 (not_7_out, L___0_R___1);
  R_L r_l_4 (.L(Left[3]), .nR(not_7_out), .L_2(L___0_R___1), .R(in_22), .out_5(r_l_4_out_5));
  Calc calc_1 (
    .in_1(in_6), .in_2(in_7), .in_3(in_8), .in_4(in_9), .in_5(in_10), .in_6(in_11), .in_7(in_12),
    .in_8(in_13), .in_9(button_out), .D(button_2_out), .out_12(calc_1_out_12), .out_13(calc_1_out_13),
    .Clear(C));
  Button button (.out(button_out));
  Button button_2 (.out(button_2_out[0]));
  Button button_3 (.out(button_2_out[1]));
  Button button_4 (.out(button_2_out[2]));
  Button button_5 (.out(button_2_out[3]));

  assign Right = {Left[0], Left[1], Left[2], Left[3]};
endmodule

module Parallel (
  input  Qin,
  input  nLoad,
  input  D,
  input  Load,
  output out_5
);

  wire and_1_out, and_2_out;

  and and_1 (and_1_out, Qin, nLoad);
  and and_2 (and_2_out, D, Load);
  or or_1 (out_5, and_1_out, and_2_out);
endmodule

module R_L (
  input  L,
  input  nR,
  input  L_2,
  input  R,
  output out_5
);

  wire and_1_out, and_2_out;

  and and_1 (and_1_out, L, nR);
  or or_1 (out_5, and_1_out, and_2_out);
  and and_2 (and_2_out, L_2, R);
endmodule

module Calc (
  input  in_1,
  input  in_2,
  input  in_3,
  input  in_4,
  input  in_5,
  input  in_6,
  input  in_7,
  input  in_8,
  input  in_9,
  input  Clear,
  input  [3:0] D,
  output [3:0] out_12,
  output [3:0] out_13
);

  wire and_1_out, and_2_out, and_3_out, and_4_out, and_5_out, d_ff_1_q, d_ff_2_q, d_ff_3_q, d_ff_4_q,
       d_ff_5_q, not_1_out, not_2_out, or_1_out, or_2_out, undriven;
  wire [7:0] adder_1_out, divider_1_out, multiplier_1_out, register_1_q, register_2_q, register_3_q,
       register_4_q, register_5_q, register_6_q, register_7_q, register_8_q, subtractor_1_out;

  or or_1 (or_1_out, in_1, in_2, in_3, in_4, in_5, in_6, in_7, in_8);
  and and_1 (and_1_out, or_1_out, not_1_out);
  D_Flip_Flop d_ff_1 (.clk(in_9), .D(in_9), .Q(d_ff_1_q), .reset(Clear));  // open: Qn, preset, en
  not not_1 (not_1_out, or_2_out);
  Register register_1 (
    .D({in_8, in_7, in_6, in_5, in_4, in_3, in_2, in_1}), .en(undriven), .Q(register_1_q), .clk(and_1_out),
    .clr(Clear));
  Register register_2 (
    .D({in_8, in_7, in_6, in_5, in_4, in_3, in_2, in_1}), .en(undriven), .Q(register_2_q), .clk(in_9),
    .clr(Clear));
  Register register_3 (
    .D({in_8, in_7, in_6, in_5, in_4, in_3, in_2, in_1}), .en(undriven), .Q(register_3_q), .clk(and_1_out),
    .clr(Clear));
  Register register_4 (
    .D({in_8, in_7, in_6, in_5, in_4, in_3, in_2, in_1}), .en(undriven), .Q(register_4_q), .clk(in_9),
    .clr(Clear));
  Register register_5 (
    .D({in_8, in_7, in_6, in_5, in_4, in_3, in_2, in_1}), .en(undriven), .Q(register_5_q), .clk(and_1_out),
    .clr(Clear));
  Register register_6 (
    .D({in_8, in_7, in_6, in_5, in_4, in_3, in_2, in_1}), .en(undriven), .Q(register_6_q), .clk(in_9),
    .clr(Clear));
  Register register_7 (
    .D({in_8, in_7, in_6, in_5, in_4, in_3, in_2, in_1}), .en(undriven), .Q(register_7_q), .clk(and_1_out),
    .clr(Clear));
  Register register_8 (
    .D({in_8, in_7, in_6, in_5, in_4, in_3, in_2, in_1}), .en(undriven), .Q(register_8_q), .clk(in_9),
    .clr(Clear));
  or or_2 (or_2_out, D[3], D[2], D[1], D[0]);
  Divider divider_1 (.a(register_1_q), .b(register_2_q), .out(divider_1_out));  // open: upper, rem
  Multiplier multiplier_1 (.a(register_3_q), .b(register_4_q), .out(multiplier_1_out));  // open: cin, cout
  Subtractor subtractor_1 (.a(register_5_q), .b(register_6_q), .out(subtractor_1_out));  // open: bin, bout
  Adder adder_1 (.a(register_7_q), .b(register_8_q), .out(adder_1_out));  // open: cin, cout
  assign out_12 = not_2_out ? {in_4, in_3, in_2, in_1} : 4'bz;  // Controlled_Buffer controlled_buffer_1
  assign out_13 = not_2_out ? {in_8, in_7, in_6, in_5} : 4'bz;  // Controlled_Buffer controlled_buffer_2
  assign out_12 = and_2_out ? divider_1_out[3:0] : 4'bz;  // Controlled_Buffer controlled_buffer_3
  assign out_13 = and_2_out ? divider_1_out[7:4] : 4'bz;  // Controlled_Buffer controlled_buffer_4
  assign out_12 = and_3_out ? multiplier_1_out[3:0] : 4'bz;  // Controlled_Buffer controlled_buffer_5
  assign out_13 = and_3_out ? multiplier_1_out[7:4] : 4'bz;  // Controlled_Buffer controlled_buffer_6
  assign out_12 = and_4_out ? subtractor_1_out[3:0] : 4'bz;  // Controlled_Buffer controlled_buffer_7
  assign out_13 = and_4_out ? subtractor_1_out[7:4] : 4'bz;  // Controlled_Buffer controlled_buffer_8
  assign out_12 = and_5_out ? adder_1_out[3:0] : 4'bz;  // Controlled_Buffer controlled_buffer_9
  assign out_13 = and_5_out ? adder_1_out[7:4] : 4'bz;  // Controlled_Buffer controlled_buffer_10
  D_Flip_Flop d_ff_2 (.clk(D[0]), .D(D[0]), .Q(d_ff_2_q), .reset(Clear));  // open: Qn, preset, en
  D_Flip_Flop d_ff_3 (.clk(D[1]), .D(D[1]), .Q(d_ff_3_q), .reset(Clear));  // open: Qn, preset, en
  D_Flip_Flop d_ff_4 (.clk(D[2]), .D(D[2]), .Q(d_ff_4_q), .reset(Clear));  // open: Qn, preset, en
  D_Flip_Flop d_ff_5 (.clk(D[3]), .D(D[3]), .Q(d_ff_5_q), .reset(Clear));  // open: Qn, preset, en
  not not_2 (not_2_out, d_ff_1_q);
  and and_2 (and_2_out, d_ff_1_q, d_ff_2_q);
  and and_3 (and_3_out, d_ff_1_q, d_ff_3_q);
  and and_4 (and_4_out, d_ff_1_q, d_ff_4_q);
  and and_5 (and_5_out, d_ff_1_q, d_ff_5_q);
endmodule
