// Logisim project Lab-6.circ as structural Verilog: 1 circuit, main circuit main
module main (
  input  A,
  input  B,
  input  C,
  input  A_2,
  input  B_2,
  input  C_2,
  input  D,
  input  A_3,
  input  B_3,
  input  C_3,
  input  D_2,
  input  A_4,
  input  B_4,
  input  C_4,
  input  D_3,
  input  A_5,
  input  B_5,
  input  C_5,
  input  D_4,
  input  A_6,
  input  B_6,
  input  C_6,
  input  D_5,
  input  A_7,
  input  B_7,
  input  C_7,
  input  D_6,
  input  A_8,
  input  B_8,
  input  C_8,
  input  D_7,
  input  A_9,
  input  B_9,
  input  C_9,
  input  D_8,
  input  A_10,
  input  B_10,
  input  C_10,
  input  D_9,
  input  A_11,
  input  B_11,
  input  C_11,
  input  D_10,
  input  A_12,
  input  B_12,
  input  C_12,
  input  D_11,
  input  A_13,
  input  B_13,
  input  C_13,
  input  D_12,
  input  A_14,
  input  B_14,
  input  C_14,
  input  A_15,
  input  B_15,
  input  C_15,
  input  D_13,
  output out_59,
  output out_60,
  output out_61,
  output out_62,
  output out_63,
  output out_64,
  output out_65,
  output out_66,
  output out_67,
  output out_68,
  output out_69,
  output out_70,
  output out_71,
  output out_72,
  output out_73
);

  wire and_1_out, and_2_out, and_3_out, and_4_out, and_5_out, and_6_out, and_7_out, and_8_out, and_9_out,
       and_10_out, and_14_out, and_17_out, and_18_out, and_19_out, and_20_out, and_21_out, and_22_out,
       and_23_out, and_24_out, and_25_out, and_26_out, and_27_out, and_28_out, and_29_out, and_31_out,
       and_32_out, buffer_1_out, nand_1_out, nand_2_out, nand_3_out, nand_4_out, nand_5_out, nand_6_out,
       nand_7_out, nand_9_out, nand_10_out, nand_11_out, nand_12_out, nand_13_out, nand_14_out, nand_15_out,
       nand_16_out, nand_17_out, nand_18_out, nand_19_out, nand_20_out, nand_21_out, nand_22_out,
       nand_23_out, nand_24_out, nand_25_out, nand_26_out, nand_27_out, nand_28_out, nand_29_out,
       nand_30_out, nand_31_out, nand_32_out, nand_33_out, nand_34_out, nand_35_out, nand_36_out,
       nand_37_out, nand_38_out, nor_1_out, nor_2_out, nor_3_out, not_1_out, not_2_out, not_3_out, not_4_out,
       not_5_out, not_6_out, not_7_out, not_8_out, not_9_out, not_10_out, not_11_out, not_12_out, not_13_out,
       not_14_out, not_15_out, not_16_out, not_17_out, not_18_out, not_19_out, not_20_out, not_21_out,
       not_22_out, not_23_out, not_24_out, not_25_out, not_26_out, not_27_out, not_28_out, not_29_out,
       not_30_out, not_31_out, not_32_out, not_33_out, not_34_out, not_35_out, not_36_out, not_37_out,
       not_38_out, not_39_out, not_40_out, not_41_out, not_42_out, or_1_out, or_2_out, or_3_out, or_4_out,
       or_6_out, or_7_out, or_8_out, or_9_out, or_10_out, or_11_out, or_12_out, or_13_out, or_14_out,
       or_16_out, or_17_out, or_18_out, or_19_out, or_21_out, or_22_out, or_23_out, or_24_out, or_25_out,
       or_28_out, or_29_out;

  not not_1 (not_1_out, B);
  not not_2 (not_2_out, B);
  not not_3 (not_3_out, C);
  not not_4 (not_4_out, A);
  not not_5 (not_5_out, A);
  not not_6 (not_6_out, C);
  not not_7 (not_7_out, A_5);
  not not_8 (not_8_out, B_5);
  not not_9 (not_9_out, C_5);
  not not_10 (not_10_out, B_5);
  not not_11 (not_11_out, C_5);
  buf buffer_1 (buffer_1_out, C_5);
  not not_12 (not_12_out, D_7);
  not not_13 (not_13_out, D_7);
  not not_14 (not_14_out, C_8);
  not not_15 (not_15_out, D_7);
  not not_16 (not_16_out, B_8);
  not not_17 (not_17_out, C_8);
  not not_18 (not_18_out, B_8);
  not not_19 (not_19_out, D_7);
  not not_20 (not_20_out, C_8);
  not not_21 (not_21_out, B_8);
  not not_22 (not_22_out, D_7);
  not not_23 (not_23_out, A_8);
  not not_24 (not_24_out, C_8);
  not not_25 (not_25_out, A_8);
  not not_26 (not_26_out, D_7);
  not not_27 (not_27_out, B_8);
  not not_28 (not_28_out, A_8);
  not not_29 (not_29_out, C_8);
  not not_30 (not_30_out, B_8);
  not not_31 (not_31_out, A_8);
  not not_32 (not_32_out, D_7);
  not not_33 (not_33_out, C_8);
  not not_34 (not_34_out, B_8);
  not not_35 (not_35_out, A_8);
  not not_36 (not_36_out, C_13);
  not not_37 (not_37_out, A_13);
  not not_38 (not_38_out, D_12);
  not not_39 (not_39_out, B_13);
  not not_40 (not_40_out, A_13);
  not not_41 (not_41_out, C_13);
  not not_42 (not_42_out, B_13);
  and and_1 (and_1_out, A, not_1_out, C);
  and and_2 (and_2_out, not_2_out, not_3_out);
  and and_3 (and_3_out, not_4_out, C);
  and and_4 (and_4_out, not_5_out, B, not_6_out);
  and and_5 (and_5_out, A, B);
  buf and_6 (and_6_out, not_7_out);  // AND_Gate
  and and_7 (and_7_out, A_5, not_8_out, not_9_out, D_4);
  and and_8 (and_8_out, not_10_out, C_5, D_4);
  and and_9 (and_9_out, not_11_out, D_4);
  and and_10 (and_10_out, A_5, buffer_1_out, D_4);
  or or_1 (or_1_out, not_12_out, C_8, B_8, A_8);
  or or_2 (or_2_out, not_13_out, not_14_out, B_8, A_8);
  or or_3 (or_3_out, not_15_out, C_8, not_16_out, A_8);
  or or_4 (or_4_out, D_7, not_17_out, not_18_out, A_8);
  or or_5 (or_4_out, not_19_out, not_20_out, not_21_out, A_8);
  or or_6 (or_6_out, not_22_out, C_8, B_8, not_23_out);
  or or_7 (or_7_out, D_7, not_24_out, B_8, not_25_out);
  or or_8 (or_8_out, not_26_out, C_8, not_27_out, not_28_out);
  or or_9 (or_9_out, D_7, not_29_out, not_30_out, not_31_out);
  or or_10 (or_10_out, not_32_out, not_33_out, not_34_out, not_35_out);
  or or_11 (or_11_out, not_36_out, B_13, not_37_out);
  or or_12 (or_12_out, not_38_out, not_39_out, A_13);
  or or_13 (or_13_out, B_13, not_40_out);
  or or_14 (or_14_out, not_41_out, A_13);
  or or_15 (out_60, and_1_out, and_2_out, and_3_out, and_4_out, and_5_out);
  and and_11 (out_67, or_1_out, or_2_out, or_3_out, or_4_out, or_4_out, or_6_out, or_7_out, or_8_out, or_9_out, or_10_out);
  and and_12 (out_71, or_11_out, or_12_out, or_13_out, or_14_out, not_42_out);
  and and_13 (out_63, and_6_out, and_7_out, and_8_out, and_9_out, and_10_out, B_5);
  and and_14 (and_14_out, ~C_4, D_3);  // AND_Gate
  or or_16 (or_16_out, C_9, ~D_8);  // OR_Gate
  or or_17 (or_17_out, A_9, ~D_8);  // OR_Gate
  or or_18 (or_18_out, ~B_9, ~C_9);  // OR_Gate
  or or_19 (or_19_out, D_8, ~C_9, ~A_9);  // OR_Gate
  and and_15 (out_70, ~C_14, ~B_14, ~A_14);  // AND_Gate
  or or_20 (out_62, ~A_4, and_14_out, ~B_4);  // OR_Gate
  and and_16 (out_66, or_16_out, or_17_out, or_18_out, or_19_out);
  and and_17 (and_17_out, ~A_2, ~B_2, C_2, D);  // AND_Gate
  and and_18 (and_18_out, ~A_2, B_2, C_2, ~D);  // AND_Gate
  and and_19 (and_19_out, ~A_2, B_2, C_2, D);  // AND_Gate
  and and_20 (and_20_out, A_2, ~B_2, ~C_2, ~D);  // AND_Gate
  and and_21 (and_21_out, A_2, ~B_2, ~C_2, D);  // AND_Gate
  and and_22 (and_22_out, A_2, ~B_2, C_2, ~D);  // AND_Gate
  and and_23 (and_23_out, A_2, ~B_2, C_2, D);  // AND_Gate
  and and_24 (and_24_out, A_2, B_2, ~C_2, ~D);  // AND_Gate
  and and_25 (and_25_out, A_2, B_2, ~C_2, D);  // AND_Gate
  and and_26 (and_26_out, A_2, B_2, C_2, ~D);  // AND_Gate
  and and_27 (and_27_out, A_2, B_2, C_2, D);
  or or_21 (or_21_out, A_6, B_6, C_6, D_5);
  or or_22 (or_22_out, A_6, B_6, C_6, ~D_5);  // OR_Gate
  or or_23 (or_23_out, A_6, B_6, ~C_6, D_5);  // OR_Gate
  or or_24 (or_24_out, A_6, ~B_6, C_6, D_5);  // OR_Gate
  or or_25 (or_25_out, A_6, ~B_6, C_6, ~D_5);  // OR_Gate
  and and_28 (and_28_out, ~A_10, ~C_10);  // AND_Gate
  and and_29 (and_29_out, ~A_10, ~B_10, ~D_9);  // AND_Gate
  nor nor_1 (nor_1_out, A_15, C_15);
  nor nor_2 (nor_2_out, A_15, B_15, D_13);
  or or_26 (out_68, and_28_out, and_29_out);
  nand nand_1 (nand_1_out, A_12, A_12);
  nand nand_2 (nand_2_out, C_12, C_12);
  nand nand_3 (nand_3_out, A_12, A_12);
  nand nand_4 (nand_4_out, B_12, B_12);
  nand nand_5 (nand_5_out, D_11, D_11);
  nor nor_3 (nor_3_out, nor_1_out, nor_2_out);
  nand nand_6 (nand_6_out, nand_1_out, nand_2_out);
  nand nand_7 (nand_7_out, nand_3_out, nand_4_out, nand_5_out);
  nor nor_4 (out_72, nor_3_out, nor_3_out);
  or or_27 (out_61, and_17_out, and_18_out, and_19_out, and_20_out, and_21_out, and_22_out, and_23_out, and_24_out, and_25_out, and_26_out, and_27_out);
  and and_30 (out_65, or_21_out, or_22_out, or_23_out, or_24_out, or_25_out);
  nand nand_8 (out_69, nand_6_out, nand_7_out);
  and and_31 (and_31_out, C_3, D_2);
  and and_32 (and_32_out, B_3, C_3);
  or or_28 (or_28_out, A_7, C_7);
  or or_29 (or_29_out, A_7, B_7, ~C_7, D_6);  // OR_Gate
  nand nand_9 (nand_9_out, A_11, A_11);
  nand nand_10 (nand_10_out, B_11, B_11);
  nand nand_11 (nand_11_out, A_11, A_11);
  nand nand_12 (nand_12_out, D_10, D_10);
  nand nand_13 (nand_13_out, A_11, A_11);
  nand nand_14 (nand_14_out, B_11, B_11);
  nand nand_15 (nand_15_out, C_11, C_11);
  nand nand_16 (nand_16_out, D_10, D_10);
  nand nand_17 (nand_17_out, B_11, B_11);
  nand nand_18 (nand_18_out, C_11, C_11);
  nand nand_19 (nand_19_out, B_11, B_11);
  nand nand_20 (nand_20_out, D_10, D_10);
  nand nand_21 (nand_21_out, B_11, B_11);
  nand nand_22 (nand_22_out, C_11, C_11);
  nand nand_23 (nand_23_out, D_10, D_10);
  nand nand_24 (nand_24_out, C_11, C_11);
  nand nand_25 (nand_25_out, D_10, D_10);
  nand nand_26 (nand_26_out, C_11, C_11);
  or or_30 (out_59, A_3, and_31_out, and_32_out);
  and and_33 (out_64, or_28_out, or_29_out);
  nand nand_27 (nand_27_out, nand_9_out, nand_10_out, C_11, D_10);
  nand nand_28 (nand_28_out, nand_11_out, B_11, C_11, nand_12_out);
  nand nand_29 (nand_29_out, nand_13_out, B_11, C_11, D_10);
  nand nand_30 (nand_30_out, A_11, nand_14_out, nand_15_out, nand_16_out);
  nand nand_31 (nand_31_out, A_11, nand_17_out, nand_18_out, D_10);
  nand nand_32 (nand_32_out, A_11, nand_19_out, C_11, nand_20_out);
  nand nand_33 (nand_33_out, A_11, nand_21_out, C_11, D_10);
  nand nand_34 (nand_34_out, A_11, B_11, nand_22_out, nand_23_out);
  nand nand_35 (nand_35_out, A_11, B_11, nand_24_out, D_10);
  nand nand_36 (nand_36_out, A_11, B_11, C_11, nand_25_out);
  nand nand_37 (nand_37_out, A_11, B_11, nand_26_out, D_10);
  nand nand_38 (nand_38_out, A_11, B_11, C_11, D_10);
  nand nand_39 (out_73, nand_27_out, nand_28_out, nand_29_out, nand_30_out, nand_31_out, nand_32_out, nand_33_out, nand_34_out, nand_35_out, nand_36_out, nand_37_out, nand_38_out);

  // Notes on the sheet:
  //   EXERCISE 1a
  //   EXERCISE 1b
  //   EXERCISE 1c
  //   EXERCISE 1d
  //   EXERCISE 1b SIMP.
  //   EXERCISE 1c SIMP
  //   EXERCISE 1d SIMP
  //   EXERCISE 2MIN
  //   EXERCISE 2MAX
  //   EXERCISE 3 
  //   EXERCISE 3 NAND 
  //   EXERCISE 3 NOR
  //   EXERCISE 2MIN SIM
  //   EXERCISE 2MAX SIM
  //   EXERCISE 2NAND
endmodule
