// Logisim project Lab-7.circ as structural Verilog: 2 circuits, main circuit main
module main (
  input  A,
  input  B,
  input  C,
  input  D,
  input  A_2,
  input  B_2,
  input  C_2,
  input  A_3,
  input  B_3,
  input  C_3,
  input  D_2,
  input  A_4,
  input  B_4,
  input  C_4,
  input  D_3,
  input  A_5,
  input  B_5,
  input  C_5,
  input  D_4,
  input  A_6,
  input  A1,
  input  B_6,
  input  B1,
  input  A_7,
  input  B_7,
  input  C_6,
  input  D_5,
  input  A1_2,
  input  B1_2,
  input  C1,
  input  D1,
  output out_32,
  output out_33,
  output out_34,
  output out_35,
  output out_36,
  output out_37
);

  wire A1_nB_nB1_out, a_2_out, a_3_out, A_B_2_out, A_B_3_out, A_B_out, A_nA1B_nB1_out, A_nB_out, a_out,
       AA1_nB1_out, AA1BB1_out, ab_2_out, ab_3_out, aB_4_out, Ab_5_out, AB_6_out, aB_7_out, Ab_8_out, aB_out,
       aBc_2_out, abC_3_out, Abc_4_out, aBc_5_out, AbC_6_out, Abc_out, aBcD_out, aBD_2_out, aBD_3_out,
       abd_4_out, aBd_out, aC_2_out, ac_3_out, AC_4_out, Ac_5_out, ac_6_out, Ac_7_out, AC_8_out, aC_out,
       acd_2_out, aCD_3_out, acd_4_out, aCD_5_out, AcD_6_out, aCd_out, Ad_2_out, aD_3_out, AD_4_out, aD_out,
       and_1_out, and_2_out, and_3_out, b_2_out, b_3_out, b_out, bC_2_out, Bc_3_out, bc_4_out, BC_5_out,
       BC_out, bCD_2_out, BcD_3_out, BCd_4_out, bcd_out, Bd_2_out, bd_out, c_2_out, c_3_out, c_out, Cd_2_out,
       cd_3_out, cD_out, d_2_out, d_3_out, d_out, e_2_out, e_3_out, e_out, f_2_out, f_3_out, f_out, g_2_out,
       g_3_out, g_out, nA1BB1_out, nA_nA1_nB_nB1_out, nA_nA1B1_out, nAA1_nBB1_out, nAB_out, not_1_out,
       not_2_out, not_3_out, not_4_out, not_6_out, not_7_out, not_8_out, not_9_out, not_10_out, not_11_out,
       not_12_out, not_13_out, not_14_out, not_15_out, not_16_out, not_17_out, not_18_out, not_19_out,
       not_20_out, or_1_out, xnor_2_out, xnor_3_out, xnor_4_out, xnor_5_out;

  not not_1 (not_1_out, A_3);
  not not_2 (not_2_out, A_4);
  not not_3 (not_3_out, B_3);
  not not_4 (not_4_out, B_4);
  or or_1 (or_1_out, C, D);
  not not_5 (out_35, D);
  not not_6 (not_6_out, C_3);
  not not_7 (not_7_out, D_2);
  not not_8 (not_8_out, D_3);
  not not_9 (not_9_out, C_4);
  and and_1 (and_1_out, B, or_1_out);
  and and_2 (and_2_out, ~B, or_1_out);  // AND_Gate
  xnor xnor_1 (out_34, C, D);
  and Abc (Abc_out, A_3, not_3_out, not_6_out);
  and aCd (aCd_out, not_1_out, C_3, not_7_out);
  and bcd (bcd_out, not_3_out, not_6_out, not_7_out);
  and aBc_2 (aBc_2_out, not_1_out, B_3, not_6_out);
  and abC_3 (abC_3_out, not_1_out, not_3_out, C_3);
  and acd_2 (acd_2_out, not_1_out, not_6_out, not_7_out);
  and aBd (aBd_out, not_1_out, B_3, not_7_out);
  and aBD_2 (aBD_2_out, not_1_out, B_3, D_2);
  and aCD_3 (aCD_3_out, not_1_out, C_3, D_2);
  and aB (aB_out, not_1_out, B_3);
  and aD (aD_out, not_1_out, D_2);
  and ab_2 (ab_2_out, not_1_out, not_3_out);
  and aC (aC_out, not_1_out, C_3);
  and aBcD (aBcD_out, not_1_out, B_3, not_6_out, D_2);
  and bd (bd_out, not_4_out, not_8_out);
  and aC_2 (aC_2_out, not_2_out, C_4);
  and BC (BC_out, B_4, C_4);
  and Ad_2 (Ad_2_out, A_4, not_8_out);
  and ab_3 (ab_3_out, not_2_out, not_4_out);
  and ac_3 (ac_3_out, not_2_out, not_9_out);
  and aD_3 (aD_3_out, not_2_out, D_3);
  and cD (cD_out, not_9_out, D_3);
  and aB_4 (aB_4_out, not_2_out, B_4);
  and Ab_5 (Ab_5_out, A_4, not_4_out);
  and Cd_2 (Cd_2_out, C_4, not_8_out);
  and AC_4 (AC_4_out, A_4, C_4);
  and AB_6 (AB_6_out, A_4, B_4);
  and cd_3 (cd_3_out, not_9_out, not_8_out);
  and Bd_2 (Bd_2_out, B_4, not_8_out);
  and bC_2 (bC_2_out, not_4_out, C_4);
  and AD_4 (AD_4_out, A_4, D_3);
  and aBD_3 (aBD_3_out, not_2_out, B_4, D_3);
  and Abc_4 (Abc_4_out, A_4, not_4_out, not_9_out);
  and acd_4 (acd_4_out, not_2_out, not_9_out, not_8_out);
  and aCD_5 (aCD_5_out, not_2_out, C_4, D_3);
  and AcD_6 (AcD_6_out, A_4, not_9_out, D_3);
  and abd_4 (abd_4_out, not_2_out, not_4_out, not_8_out);
  and bCD_2 (bCD_2_out, not_4_out, C_4, D_3);
  and BcD_3 (BcD_3_out, B_4, not_9_out, D_3);
  and BCd_4 (BCd_4_out, B_4, C_4, not_8_out);
  and aBc_5 (aBc_5_out, not_2_out, B_4, not_9_out);
  and Ac_5 (Ac_5_out, not_9_out, A_4);
  and and_3 (and_3_out, B, ~C, out_35);  // AND_Gate
  or or_2 (out_32, A, and_1_out);
  or or_3 (out_33, and_2_out, and_3_out);
  or u_a (a_out, aC_out, aBD_2_out, bcd_out, Abc_out);
  or u_b (b_out, ab_2_out, acd_2_out, aCD_3_out, Abc_out);
  or u_c (c_out, aB_out, aD_out, bcd_out, Abc_out);
  or u_d (d_out, aCd_out, abC_3_out, bcd_out, Abc_out, aBcD_out);
  or e (e_out, aCd_out, bcd_out);
  or f (f_out, aBc_2_out, acd_2_out, aBd_out, Abc_out);
  or g (g_out, aCd_out, abC_3_out, aBc_2_out, Abc_out);
  _7_Segment_Display u_7_segment_display_1 (
    .g(g_out), .f(f_out), .a(a_out), .b(b_out), .e(e_out), .d(d_out), .c(c_out));  // open: dp
  not not_10 (not_10_out, A_2);
  or u_a_2 (a_2_out, bd_out, aC_2_out, aBD_3_out, BC_out, Abc_4_out, Ad_2_out);
  or u_b_2 (b_2_out, ab_3_out, acd_4_out, bd_out, aCD_5_out, AcD_6_out);
  or u_c_2 (c_2_out, ac_3_out, aD_3_out, cD_out, aB_4_out, Ab_5_out);
  or u_d_2 (d_2_out, abd_4_out, bCD_2_out, BcD_3_out, BCd_4_out, Ac_5_out);
  or e_2 (e_2_out, bd_out, Cd_2_out, AC_4_out, AB_6_out);
  or f_2 (f_2_out, cd_3_out, aBc_5_out, Bd_2_out, Ab_5_out, AC_4_out);
  or g_2 (g_2_out, bC_2_out, Cd_2_out, aBc_5_out, Ab_5_out, AD_4_out);
  not not_11 (not_11_out, B_2);
  not not_12 (not_12_out, C_2);
  _7_Segment_Display u_7_segment_display_2 (
    .g(g_2_out), .f(f_2_out), .a(a_2_out), .b(b_2_out), .e(e_2_out), .d(d_2_out), .c(c_2_out));  // open: dp
  and ac_6 (ac_6_out, not_10_out, not_12_out);
  and Ac_7 (Ac_7_out, A_2, not_12_out);
  and Bc_3 (Bc_3_out, B_2, not_12_out);
  and AC_8 (AC_8_out, A_2, C_2);
  and bc_4 (bc_4_out, not_11_out, not_12_out);
  and BC_5 (BC_5_out, B_2, C_2);
  and aB_7 (aB_7_out, not_10_out, B_2);
  and Ab_8 (Ab_8_out, A_2, not_11_out);
  and AbC_6 (AbC_6_out, A_2, not_11_out, C_2);
  or u_a_3 (a_3_out, ac_6_out, B_2, AC_8_out);
  or u_b_3 (b_3_out, not_10_out, bc_4_out, BC_5_out);
  or u_c_3 (c_3_out, not_11_out, C_2, A_2);
  or u_d_3 (d_3_out, ac_6_out, aB_7_out, Bc_3_out, AbC_6_out);
  or e_3 (e_3_out, ac_6_out, Bc_3_out);
  or f_3 (f_3_out, bc_4_out, Ab_8_out, Ac_7_out);
  or g_3 (g_3_out, aB_7_out, Ab_8_out, Ac_7_out);
  not not_13 (not_13_out, A_5);
  not not_14 (not_14_out, A_6);
  not not_15 (not_15_out, A1);
  _7_Segment_Display u_7_segment_display_3 (
    .g(g_3_out), .f(f_3_out), .a(a_3_out), .b(b_3_out), .e(e_3_out), .d(d_3_out), .c(c_3_out));  // open: dp
  not not_16 (not_16_out, B_5);
  not not_17 (not_17_out, C_5);
  not not_18 (not_18_out, B_6);
  not not_19 (not_19_out, D_4);
  not not_20 (not_20_out, B1);
  ExactlyOne xor_1 (.out(out_36), .in0(A_5), .in1(B_5), .in2(C_5), .in3(D_4));
  and nA_nA1B1 (nA_nA1B1_out, not_14_out, not_15_out, B1);
  and nAB (nAB_out, not_14_out, B_6);
  and nA1BB1 (nA1BB1_out, not_15_out, B_6, B1);
  and nA_nA1_nB_nB1 (nA_nA1_nB_nB1_out, not_14_out, not_15_out, not_18_out, not_20_out);
  and nAA1_nBB1 (nAA1_nBB1_out, not_14_out, A1, not_18_out, B1);
  and A_nA1B_nB1 (A_nA1B_nB1_out, A_6, not_15_out, B_6, not_20_out);
  and AA1BB1 (AA1BB1_out, A_6, A1, B_6, B1);
  and A1_nB_nB1 (A1_nB_nB1_out, A1, not_18_out, not_20_out);
  and A_nB (A_nB_out, A_6, not_18_out);
  and AA1_nB1 (AA1_nB1_out, A_6, A1, not_20_out);
  xnor xnor_2 (xnor_2_out, A_7, A1_2);
  xnor xnor_3 (xnor_3_out, B_7, B1_2);
  xnor xnor_4 (xnor_4_out, C_6, C1);
  xnor xnor_5 (xnor_5_out, D_5, D1);
  or A_B (A_B_out, nA_nA1B1_out, nAB_out, nA1BB1_out);
  LED led_1 (.in(A_B_out));
  LED led_2 (.in(A_B_2_out));
  or A_B_2 (A_B_2_out, nA_nA1_nB_nB1_out, nAA1_nBB1_out, A_nA1B_nB1_out, AA1BB1_out);
  or A_B_3 (A_B_3_out, A1_nB_nB1_out, A_nB_out, AA1_nB1_out);
  LED led_3 (.in(A_B_3_out));
  and and_4 (out_37, xnor_2_out, xnor_3_out, xnor_4_out, xnor_5_out);

  // Notes on the sheet:
  //   Lab Ex 1.)
  //   Lab Ex. 2 Decimal
  //   Lab Ex. 2 Hexa
  //   Lab Ex.2 Octal
  //   4-Bit Parity Gen
  //   2-Bit Comparator
  //   4 Bit Equality 
endmodule

module Hexa (
  input  A,
  input  B,
  input  C,
  input  D,
  output a_2,
  output b_2,
  output c_2,
  output d_2,
  output e,
  output f,
  output g
);

  wire and_1_out, and_2_out, and_3_out, and_4_out, and_5_out, and_6_out, and_7_out, and_8_out, and_9_out,
       and_10_out, and_11_out, and_12_out, and_13_out, and_14_out, and_15_out, and_16_out, and_17_out,
       and_18_out, and_19_out, and_20_out, and_21_out, and_22_out, and_23_out, and_24_out, and_25_out,
       and_26_out, and_27_out, and_28_out, and_29_out, and_30_out, and_31_out, and_32_out, and_33_out,
       and_34_out, and_35_out, not_1_out, not_2_out, not_3_out, not_4_out, not_5_out, not_6_out, not_7_out,
       not_8_out, not_9_out, not_10_out, not_11_out, not_12_out, not_13_out, not_14_out, not_15_out,
       not_16_out, not_17_out, not_18_out, not_19_out, not_20_out, not_21_out, not_22_out, not_23_out,
       not_24_out, not_25_out, not_26_out, not_27_out, not_28_out, not_29_out, not_30_out, not_31_out,
       not_32_out, not_33_out, not_34_out, not_35_out, not_36_out, not_37_out, not_38_out, not_39_out,
       not_40_out, not_41_out, not_42_out, not_43_out;

  not not_1 (not_1_out, B);
  and and_1 (and_1_out, not_1_out, not_2_out);
  not not_2 (not_2_out, D);
  not not_3 (not_3_out, A);
  and and_2 (and_2_out, not_3_out, C);
  not not_4 (not_4_out, A);
  and and_3 (and_3_out, not_4_out, B, D);
  and and_4 (and_4_out, B, C);
  and and_5 (and_5_out, A, not_5_out, not_6_out);
  not not_5 (not_5_out, B);
  not not_6 (not_6_out, C);
  and and_6 (and_6_out, A, not_7_out);
  not not_7 (not_7_out, D);
  not not_8 (not_8_out, A);
  and and_7 (and_7_out, not_8_out, not_9_out);
  not not_9 (not_9_out, B);
  not not_10 (not_10_out, A);
  and and_8 (and_8_out, not_10_out, not_11_out, not_12_out);
  not not_11 (not_11_out, C);
  not not_12 (not_12_out, D);
  not not_13 (not_13_out, B);
  and and_9 (and_9_out, not_13_out, not_14_out);
  not not_14 (not_14_out, D);
  not not_15 (not_15_out, A);
  and and_10 (and_10_out, not_15_out, C, D);
  and and_11 (and_11_out, A, not_16_out, D);
  not not_16 (not_16_out, C);
  not not_17 (not_17_out, A);
  and and_12 (and_12_out, not_17_out, not_18_out);
  not not_18 (not_18_out, C);
  not not_19 (not_19_out, A);
  and and_13 (and_13_out, not_19_out, D);
  not not_20 (not_20_out, C);
  and and_14 (and_14_out, not_20_out, D);
  not not_21 (not_21_out, A);
  and and_15 (and_15_out, not_21_out, B);
  and and_16 (and_16_out, A, not_22_out);
  not not_22 (not_22_out, B);
  not not_23 (not_23_out, A);
  and and_17 (and_17_out, not_23_out, not_24_out, not_25_out);
  not not_24 (not_24_out, B);
  not not_25 (not_25_out, D);
  not not_26 (not_26_out, B);
  and and_18 (and_18_out, not_26_out, C, D);
  not not_27 (not_27_out, C);
  and and_19 (and_19_out, B, not_27_out, D);
  and and_20 (and_20_out, B, C, not_28_out);
  not not_28 (not_28_out, D);
  and and_21 (and_21_out, A, not_29_out);
  not not_29 (not_29_out, C);
  not not_30 (not_30_out, B);
  and and_22 (and_22_out, not_30_out, not_31_out);
  not not_31 (not_31_out, D);
  and and_23 (and_23_out, C, not_32_out);
  not not_32 (not_32_out, D);
  and and_24 (and_24_out, A, C);
  and and_25 (and_25_out, A, B);
  not not_33 (not_33_out, C);
  and and_26 (and_26_out, not_33_out, not_34_out);
  not not_34 (not_34_out, D);
  not not_35 (not_35_out, A);
  and and_27 (and_27_out, not_35_out, B, not_36_out);
  not not_36 (not_36_out, C);
  and and_28 (and_28_out, B, not_37_out);
  not not_37 (not_37_out, D);
  and and_29 (and_29_out, A, not_38_out);
  not not_38 (not_38_out, B);
  and and_30 (and_30_out, A, C);
  not not_39 (not_39_out, B);
  and and_31 (and_31_out, not_39_out, C);
  and and_32 (and_32_out, C, not_40_out);
  not not_40 (not_40_out, D);
  not not_41 (not_41_out, A);
  and and_33 (and_33_out, not_41_out, B, not_42_out);
  not not_42 (not_42_out, C);
  and and_34 (and_34_out, A, not_43_out);
  not not_43 (not_43_out, B);
  and and_35 (and_35_out, A, D);
  or or_1 (b_2, and_7_out, and_8_out, and_9_out, and_10_out, and_11_out);
  or or_2 (c_2, and_12_out, and_13_out, and_14_out, and_15_out, and_16_out);
  or or_3 (d_2, and_17_out, and_18_out, and_19_out, and_20_out, and_21_out);
  or or_4 (e, and_22_out, and_23_out, and_24_out, and_25_out);
  or or_5 (f, and_26_out, and_27_out, and_28_out, and_29_out, and_30_out);
  or or_6 (g, and_31_out, and_32_out, and_33_out, and_34_out, and_35_out);
  or or_7 (a_2, and_1_out, and_2_out, and_3_out, and_4_out, and_5_out, and_6_out);
endmodule
